# Fritzing sketch fritzing-monitor-pool (saved by Fritzing 1.0.2b)
breadboards: 2

parts:
  TinyPICO = TinyPICO
  Waveshare_e-Paper = Waveshare e-Paper HAT [package=THT]
  Adafruit_MAX31856 = Adafruit MAX31856 Thermocouple Amp [part_number="Adafruit #3263"]
  Battery = LIPO-110mAh [package=lipo-110]

nets:
  3V3: TinyPICO.3V3, Waveshare_e-Paper.pin_8, Adafruit_MAX31856.VIN
  N1: TinyPICO.GND, Waveshare_e-Paper.pin_7, Battery.-
  N2: TinyPICO.BAT, Battery.+
  N3: TinyPICO.33, Adafruit_MAX31856.!CS
  N4: TinyPICO.32, Waveshare_e-Paper.pin_1
  N5: TinyPICO.21, Waveshare_e-Paper.pin_2
  N6: TinyPICO.22, Waveshare_e-Paper.pin_3
  N7: TinyPICO.5, Waveshare_e-Paper.pin_4
  N8: TinyPICO.18, Waveshare_e-Paper.pin_5, Adafruit_MAX31856.SCK
  N9: TinyPICO.19, Adafruit_MAX31856.SDO
  N10: TinyPICO.23, Waveshare_e-Paper.pin_6, Adafruit_MAX31856.SDI

custom parts:
  TinyPICO: TinyPICO ESP32 by Unexpected Maker
  Waveshare e-Paper HAT: .This is a universal driver board for e-Paper raw panels, can be used to drive various SPI interface e-Paper from Waveshare.
  Adafruit MAX31856 Thermocouple Amp: Thermocouples are very sensitive, requiring a good amplifier with a cold-compensation reference, as well as calculations to handle any non-linearities. For a long time we've suggested our MAX31855K breakout, which works great but is only for K-type thermocouples. Now we're happy to offer a great new thermocouple amplifier/converter that can handle just about any type of thermocouple, and even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
